# Fritzing sketch BinaryCalculatorFritzing (saved by Fritzing 0.9.3b)
breadboards: 1

parts:
  Part1 = Arduino Uno (Rev3) - ICSP
  LED1 = LED - 5mm [color="Red (633nm)" package="5 mm [THT]"]
  LED2 = LED - 5mm [color="Red (633nm)" package="5 mm [THT]"]
  LED3 = LED - 5mm [color="Red (633nm)" package="5 mm [THT]"]
  LED4 = LED - 5mm [color="Red (633nm)" package="5 mm [THT]"]
  LED5 = LED - 5mm [color="Red (633nm)" package="5 mm [THT]"]
  LED6 = LED - 5mm [color="Red (633nm)" package="5 mm [THT]"]
  LED7 = LED - 5mm [color="Red (633nm)" package="5 mm [THT]"]
  LED8 = LED - 5mm [color="Red (633nm)" package="5 mm [THT]"]
  R1 = Resistor [tolerance=±5% resistance=330 package=THT]
  R2 = Resistor [tolerance=±5% resistance=330 package=THT]
  R3 = Resistor [tolerance=±5% resistance=330 package=THT]
  R4 = Resistor [tolerance=±5% resistance=330 package=THT]
  R5 = Resistor [tolerance=±5% resistance=330 package=THT]
  R6 = Resistor [tolerance=±5% resistance=330 package=THT]
  R7 = Resistor [tolerance=±5% resistance=330 package=THT]
  R8 = Resistor [tolerance=±5% resistance=330 package=THT]

nets:
  N1: Part1.D8, LED7.anode
  N2: Part1.D9_PWM, LED8.anode
  N3: Part1.D2, LED1.anode
  N4: Part1.D3_PWM, LED2.anode
  N5: Part1.D4, LED3.anode
  N6: Part1.D5_PWM, LED4.anode
  N7: Part1.D6_PWM, LED5.anode
  N8: Part1.D7, LED6.anode
  N9: Part1.GND, R1.Pin_1, R2.Pin_1, R3.Pin_1, R4.Pin_1, R5.Pin_1, R6.Pin_1, R7.Pin_1, R8.Pin_1
  N10: LED1.cathode, R1.Pin_0
  N11: LED2.cathode, R2.Pin_0
  N12: LED3.cathode, R3.Pin_0
  N13: LED4.cathode, R4.Pin_0
  N14: LED5.cathode, R5.Pin_0
  N15: LED6.cathode, R6.Pin_0
  N16: LED7.cathode, R7.Pin_0
  N17: LED8.cathode, R8.Pin_0

notes:
  Binary system represented by LEDs:
  0. 2^0 = 1
  1. 2^1 = 2
  2. 2^2 = 4
  3. 2^3 = 8
  4. 2^4 = 16
  5. 2^5 = 32
  6. 2^6 = 64
  7. 2^7 = 128
